// Logisim project PacMo.circ as structural Verilog: 1 circuit, main circuit main
module main (
  input  [1:0] ReadReg1,
  input  [1:0] ReadReg2,
  output [15:0] out_3,
  output [15:0] RegData1,
  output [15:0] out_5,
  output [15:0] RegData2,
  output [1:0] out_7,
  output [15:0] out_8,
  output [15:0] out_9,
  output [15:0] out_10,
  output [15:0] out_11
);

  wire and_1_out, and_2_out, and_3_out, and_4_out, Clock1_out, clock_1_out, comparator_1_eq, comparator_2_eq,
       decoder_1_out0, decoder_1_out1, decoder_1_out2, decoder_1_out3, decoder_2_out0, decoder_2_out1,
       decoder_2_out2, decoder_2_out3, or_1_out;
  wire [7:0] adder_1_out, Instruction_Memory_dout_2, PC_q;
  wire [15:0] Instruction_Memory_dout, subtractor_1_out, X0_q, X1_q, X2_q, X3_q;

  RAM #(.dataWidth(16)) Instruction_Memory (
    .addr(PC_q), .we(1'b0), .oe(1'b1), .clk(Clock1_out),
    .dout({Instruction_Memory_dout[15:14], out_7, Instruction_Memory_dout_2, Instruction_Memory_dout[3:0]}));  // open: din
  Clock Clock1 (.out(Clock1_out));
  Register PC (.D(adder_1_out), .clk(Clock1_out), .Q(PC_q));  // open: en, clr
  Adder adder_1 (.a(PC_q), .b(8'h1), .out(adder_1_out));  // open: cin, cout
  Decoder #(.enable("false"), .select(2)) decoder_1 (
    .out0(decoder_1_out0), .out1(decoder_1_out1), .out2(decoder_1_out2), .out3(decoder_1_out3),
    .sel(Instruction_Memory_dout[15:14]));
  Decoder #(.enable("false"), .select(2)) decoder_2 (
    .out0(decoder_2_out0), .out1(decoder_2_out1), .out2(decoder_2_out2), .out3(decoder_2_out3),
    .sel(Instruction_Memory_dout[1:0]));
  or or_1 (or_1_out, decoder_1_out0, decoder_1_out1, decoder_1_out2);
  Comparator comparator_1 (.a({8{1'b0}}), .b(PC_q), .eq(comparator_1_eq));  // open: gt, lt
  and and_1 (and_1_out, or_1_out, decoder_2_out0);
  and and_2 (and_2_out, or_1_out, decoder_2_out1);
  and and_3 (and_3_out, or_1_out, decoder_2_out2);
  and and_4 (and_4_out, or_1_out, decoder_2_out3);
  Register #(.width(16)) X0 (.D(out_10), .en(and_1_out), .clk(Clock1_out), .Q(X0_q), .clr(comparator_1_eq));
  Register #(.width(16)) X1 (.D(out_10), .en(and_2_out), .clk(Clock1_out), .Q(X1_q), .clr(comparator_1_eq));
  Register #(.width(16)) X2 (.D(out_10), .en(and_3_out), .clk(Clock1_out), .Q(X2_q), .clr(comparator_1_eq));
  Register #(.width(16)) X3 (.D(out_10), .en(and_4_out), .clk(Clock1_out), .Q(X3_q), .clr(comparator_1_eq));
  Multiplexer #(.select(2), .width(16)) multiplexer_1 (
    .in0(X0_q), .in1(X1_q), .in2(X2_q), .in3(X3_q), .out(RegData1), .sel(Instruction_Memory_dout[3:2]));
  Multiplexer #(.select(2), .width(16)) multiplexer_2 (
    .in0(X0_q), .in1(X1_q), .in2(X2_q), .in3(X3_q), .out(RegData2), .sel(out_7));
  assign out_11 = {{6{out_7[1]}}, {out_7, Instruction_Memory_dout_2}};  // Bit_Extender bit_extender_1
  Comparator comparator_2 (.a(8'hf0), .b(Instruction_Memory_dout_2), .eq(comparator_2_eq));  // open: gt, lt
  Multiplexer #(.width(16)) multiplexer_3 (.in0(out_11), .in1(RegData2), .out(out_8), .sel(comparator_2_eq));
  Adder #(.width(16)) adder_2 (.a(RegData1), .b(out_8), .out(out_3));  // open: cin, cout
  Subtractor #(.width(16)) subtractor_1 (.a(RegData1), .b(out_8), .out(subtractor_1_out));  // open: bin, bout
  Multiplexer #(.width(16)) multiplexer_4 (.in0(out_3), .in1(subtractor_1_out), .out(out_5), .sel(decoder_1_out1));
  Clock #(.phaseOffset(1)) clock_1 (.out(clock_1_out));
  RAM #(.addrWidth(16), .dataWidth(16)) Data_Memory (
    .addr(out_5), .we(decoder_1_out3), .oe(decoder_1_out2), .clk(clock_1_out), .din(RegData1), .dout(out_9));
  Hex_Digit_Display hex_digit_display_1 (.value(out_5[15:12]));  // open: dp
  Hex_Digit_Display hex_digit_display_2 (.value(out_5[11:8]));  // open: dp
  Hex_Digit_Display hex_digit_display_3 (.value(out_5[7:4]));  // open: dp
  Hex_Digit_Display hex_digit_display_4 (.value(out_5[3:0]));  // open: dp
  Multiplexer #(.width(16)) multiplexer_5 (.in0(out_5), .in1(out_9), .out(out_10), .sel(decoder_1_out2));

  // Notes on the sheet:
  //   Jake Paccione & Matthew Mohamed | Lab 8
  //   I pledge my honor that I have abided by the Stevens Honor System.
  //   Opcode
  //   ALUop
  //   Write Port
  //   MemRead
  //   MemWrite
  //   MemToReg
  //   RegWrite
  //   ReadReg1
  //   ReadReg2
  //   Read Port 1
  //   Read Port 2
endmodule
